// Logisim project licznik_mod_12.circ as structural Verilog: 1 circuit, main circuit main
module main (
);

  wire and_1_out, clock_1_out, nor_1_out, nor_2_out, not_1_out, not_2_out, t_ff_1_qn, t_ff_2_qn, t_ff_3_qn;
  wire [3:0] t_ff_1_q;

  Clock clock_1 (.out(clock_1_out));
  T_Flip_Flop t_ff_1 (.clk(clock_1_out), .T(1'b1), .Q(t_ff_1_q[0]), .Qn(t_ff_1_qn), .reset(nor_2_out));  // open: preset
  T_Flip_Flop t_ff_2 (.clk(t_ff_1_qn), .T(1'b1), .Q(t_ff_1_q[1]), .Qn(t_ff_2_qn), .reset(nor_2_out));  // open: preset
  T_Flip_Flop t_ff_3 (.clk(t_ff_2_qn), .T(1'b1), .Q(t_ff_1_q[2]), .Qn(t_ff_3_qn), .reset(nor_2_out));  // open: preset
  T_Flip_Flop t_ff_4 (.clk(t_ff_3_qn), .T(1'b1), .Q(t_ff_1_q[3]), .reset(nor_2_out));  // open: Qn, preset
  Hex_Digit_Display hex_digit_display_1 (.value(t_ff_1_q));  // open: dp
  not not_1 (not_1_out, t_ff_1_q[1]);
  not not_2 (not_2_out, t_ff_1_q[0]);
  and and_1 (and_1_out, t_ff_1_q[3], t_ff_1_q[2], not_1_out, not_2_out);
  nor nor_1 (nor_1_out, and_1_out, nor_2_out);
  nor nor_2 (nor_2_out, nor_1_out, clock_1_out);
endmodule
