// Logisim project 2x3x2_T_async.circ as structural Verilog: 1 circuit, main circuit main
module main (
);

  wire clock_1_out, or_1_out, t_ff_1_qn, t_ff_3_qn;
  wire [3:0] t_ff_1_q;

  Clock clock_1 (.out(clock_1_out));
  T_Flip_Flop t_ff_1 (.T(1'b1), .clk(clock_1_out), .Q(t_ff_1_q[0]), .Qn(t_ff_1_qn));  // open: reset, preset
  Hex_Digit_Display hex_digit_display_1 (.value(t_ff_1_q));  // open: dp
  T_Flip_Flop t_ff_2 (.T(t_ff_3_qn), .clk(t_ff_1_qn), .Q(t_ff_1_q[1]));  // open: Qn, reset, preset
  T_Flip_Flop t_ff_3 (.T(or_1_out), .clk(t_ff_1_qn), .Q(t_ff_1_q[2]), .Qn(t_ff_3_qn));  // open: reset, preset
  or or_1 (or_1_out, t_ff_1_q[1], t_ff_1_q[2]);
  T_Flip_Flop t_ff_4 (.T(1'b1), .clk(t_ff_3_qn), .Q(t_ff_1_q[3]));  // open: Qn, reset, preset
endmodule
