// Logisim project 4x3x2_D_sync.circ as structural Verilog: 1 circuit, main circuit main
module main (
  input  in_1
);

  wire and_1_out, and_2_out, and_3_out, and_4_out, and_5_out, clock_1_out, d_ff_1_q, d_ff_2_q, d_ff_3_q,
       d_ff_4_q, d_ff_4_qn, d_ff_5_q, not_1_out, not_2_out, or_1_out, xor_1_out, xor_2_out, xor_3_out,
       xor_4_out;

  Clock clock_1 (.out(clock_1_out));
  D_Flip_Flop d_ff_1 (.D(xor_1_out), .clk(clock_1_out), .Q(d_ff_1_q));  // open: Qn, preset, reset
  xor xor_1 (xor_1_out, d_ff_1_q, in_1);
  D_Flip_Flop d_ff_2 (.D(xor_2_out), .clk(clock_1_out), .Q(d_ff_2_q));  // open: Qn, preset, reset
  xor xor_2 (xor_2_out, d_ff_2_q, d_ff_1_q);
  and and_1 (and_1_out, d_ff_1_q, d_ff_2_q);
  xor xor_3 (xor_3_out, and_1_out, d_ff_3_q);
  not not_1 (not_1_out, and_1_out);
  and and_2 (and_2_out, not_1_out, d_ff_4_q);
  and and_3 (and_3_out, and_1_out, d_ff_3_q);
  D_Flip_Flop d_ff_3 (.D(and_4_out), .clk(clock_1_out), .Q(d_ff_3_q));  // open: Qn, preset, reset
  and and_4 (and_4_out, xor_3_out, d_ff_4_qn);
  D_Flip_Flop d_ff_4 (.D(or_1_out), .clk(clock_1_out), .Q(d_ff_4_q), .Qn(d_ff_4_qn));  // open: preset, reset
  or or_1 (or_1_out, and_2_out, and_3_out);
  not not_2 (not_2_out, d_ff_3_q);
  D_Flip_Flop d_ff_5 (.D(xor_4_out), .clk(clock_1_out), .Q(d_ff_5_q));  // open: Qn, preset, reset
  xor xor_4 (xor_4_out, d_ff_5_q, and_5_out);
  and and_5 (and_5_out, and_1_out, d_ff_4_q, not_2_out);

  // Notes on the sheet:
  //   d0
  //   d1
endmodule
