// Logisim project async.circ as structural Verilog: 1 circuit, main circuit main
module main (
  input  in_1,
  input  in_2
);

  wire and_1_out, and_2_out, and_3_out, clock_1_out, clock_2_out, d_ff_1_qn, d_ff_2_qn, d_ff_3_qn, d_ff_4_qn,
       nor_1_out, nor_2_out, nor_3_out, nor_4_out, not_1_out, not_2_out, not_3_out, not_4_out, not_5_out,
       not_6_out, t_ff_1_qn, t_ff_2_qn, t_ff_3_qn;
  wire [3:0] d_ff_1_q, t_ff_1_q;

  T_Flip_Flop t_ff_1 (.T(in_1), .clk(clock_1_out), .Q(t_ff_1_q[0]), .Qn(t_ff_1_qn), .reset(nor_2_out));  // open: preset
  Clock clock_1 (.out(clock_1_out));
  not not_1 (not_1_out, clock_1_out);
  and and_1 (and_1_out, d_ff_1_qn, in_2);
  Clock clock_2 (.out(clock_2_out));
  not not_2 (not_2_out, clock_2_out);
  Hex_Digit_Display hex_digit_display_1 (.value(t_ff_1_q));  // open: dp
  Hex_Digit_Display hex_digit_display_2 (.value(d_ff_1_q));  // open: dp
  D_Flip_Flop d_ff_1 (
    .D(and_1_out), .clk(clock_2_out), .Q(d_ff_1_q[0]), .Qn(d_ff_1_qn), .reset(nor_4_out));  // open: preset
  T_Flip_Flop t_ff_2 (.T(in_1), .clk(t_ff_1_qn), .Q(t_ff_1_q[1]), .Qn(t_ff_2_qn), .reset(nor_2_out));  // open: preset
  D_Flip_Flop d_ff_2 (
    .D(d_ff_2_qn), .clk(d_ff_1_qn), .Q(d_ff_1_q[1]), .Qn(d_ff_2_qn), .reset(nor_4_out));  // open: preset
  T_Flip_Flop t_ff_3 (.T(in_1), .clk(t_ff_2_qn), .Q(t_ff_1_q[2]), .Qn(t_ff_3_qn), .reset(nor_2_out));  // open: preset
  D_Flip_Flop d_ff_3 (
    .D(d_ff_3_qn), .clk(d_ff_2_qn), .Q(d_ff_1_q[2]), .Qn(d_ff_3_qn), .reset(nor_4_out));  // open: preset
  T_Flip_Flop t_ff_4 (.T(in_1), .clk(t_ff_3_qn), .Q(t_ff_1_q[3]), .reset(nor_2_out));  // open: Qn, preset
  D_Flip_Flop d_ff_4 (
    .D(d_ff_4_qn), .clk(d_ff_3_qn), .Q(d_ff_1_q[3]), .Qn(d_ff_4_qn), .reset(nor_4_out));  // open: preset
  not not_3 (not_3_out, t_ff_1_q[2]);
  and and_2 (and_2_out, t_ff_1_q[3], not_3_out, t_ff_1_q[1], not_4_out);
  not not_4 (not_4_out, t_ff_1_q[0]);
  not not_5 (not_5_out, d_ff_1_q[2]);
  not not_6 (not_6_out, d_ff_1_q[0]);
  nor nor_1 (nor_1_out, and_2_out, nor_2_out);
  nor nor_2 (nor_2_out, nor_1_out, not_1_out);
  and and_3 (and_3_out, d_ff_1_q[3], not_5_out, d_ff_1_q[1], not_6_out);
  nor nor_3 (nor_3_out, and_3_out, nor_4_out);
  nor nor_4 (nor_4_out, nor_3_out, not_2_out);
endmodule
