// Logisim project dzielenie.circ as structural Verilog: 1 circuit, main circuit main
module main (
  input  LS,
  input  MUX,
  input  in_3,
  input  clk,
  input  LA,
  input  LB,
  input  in_7,
  input  in_8,
  output B_zero,
  output sign_b,
  output sign_a,
  output koniec
);

  wire register_3_q, xor_2_out;
  wire [6:0] register_1_q, register_2_q;
  wire [7:0] adder_1_out, multiplexer_1_out, multiplexer_2_out, multiplexer_3_out, multiplexer_4_out,
       not_1_out, undriven, undriven_2;

  // DipSwitch dipswitch_1: pin names not known
  Multiplexer #(.width(8)) multiplexer_1 (.in0(adder_1_out), .in1(undriven), .out(multiplexer_1_out), .sel(MUX));
  Register register_1 (.D(multiplexer_1_out), .en(LA), .clk(clk), .Q({sign_a, register_1_q}));  // open: clr
  Multiplexer #(.width(8)) multiplexer_2 (
    .in0({sign_a, register_1_q}), .in1({8{1'b0}}), .out(multiplexer_2_out), .sel(in_7));
  // DipSwitch dipswitch_2: pin names not known
  Multiplexer #(.width(8)) multiplexer_3 (.in0(adder_1_out), .in1(undriven_2), .out(multiplexer_3_out), .sel(MUX));
  Register register_2 (.D(multiplexer_3_out), .en(LB), .clk(clk), .Q({sign_b, register_2_q}));  // open: clr
  assign not_1_out = ~multiplexer_4_out;  // NOT_Gate not_1, 8 bits wide
  Adder adder_1 (.a(not_1_out), .b(multiplexer_2_out), .out(adder_1_out), .cin(1'b1));  // open: cout
  Multiplexer #(.width(8)) multiplexer_4 (
    .in0({sign_a, register_1_q}), .in1({sign_b, register_2_q}), .out(multiplexer_4_out), .sel(in_8));
  xor xor_1 (koniec, adder_1_out[7], sign_a);
  Register #(.width(1)) register_3 (.D(xor_2_out), .en(LS), .clk(clk), .Q(register_3_q));  // open: clr
  xor xor_2 (xor_2_out, undriven_2[7], undriven[7]);
  nor nor_1 (B_zero, register_2_q[0], register_2_q[1], register_2_q[2], register_2_q[3], register_2_q[4], register_2_q[5], register_2_q[6], sign_b);
  Counter counter_1 (.load(in_3), .up(1'b1), .clk(clk), .D({8{1'b0}}));  // open: clr, count, carry, Q
endmodule
