// Logisim project licznik_wegla.circ as structural Verilog: 5 circuits, main circuit main
module main (
  input  in_1,
  input  in_2
);

  wire and_1_out, and_2_out, and_3_out, and_4_out, and_5_out, and_6_out, and_7_out, clock_1_out, not_1_out,
       not_2_out, not_3_out, not_4_out, not_5_out, not_6_out, not_7_out, not_8_out, not_9_out, or_1_out,
       or_2_out;
  wire [3:0] licznik_1_out_4, licznik_2_out_4, licznik_3_out_4, licznik_4_out_4, licznik_5_out_4;

  Clock clock_1 (.out(clock_1_out));
  Hex_Digit_Display hex_digit_display_1 (.value(licznik_2_out_4));  // open: dp
  Hex_Digit_Display hex_digit_display_2 (.value(licznik_1_out_4));  // open: dp
  licznik licznik_1 (.EN(in_1), .clk(clock_1_out), .reset(in_2), .out_4(licznik_1_out_4));
  not not_1 (not_1_out, licznik_1_out_4[1]);
  not not_2 (not_2_out, licznik_1_out_4[2]);
  and and_1 (and_1_out, licznik_1_out_4[0], not_1_out, not_2_out, licznik_1_out_4[3]);
  or or_1 (or_1_out, and_2_out, in_2);
  not not_3 (not_3_out, licznik_2_out_4[0]);
  not not_4 (not_4_out, licznik_2_out_4[1]);
  not not_5 (not_5_out, licznik_2_out_4[3]);
  licznik licznik_2 (.EN(and_1_out), .clk(clock_1_out), .reset(or_1_out), .out_4(licznik_2_out_4));
  and and_2 (and_2_out, and_1_out, and_3_out);
  and and_3 (and_3_out, not_3_out, not_4_out, licznik_2_out_4[2], not_5_out);
  licznik licznik_3 (.EN(and_2_out), .clk(clock_1_out), .reset(in_2), .out_4(licznik_3_out_4));
  not not_6 (not_6_out, licznik_3_out_4[1]);
  not not_7 (not_7_out, licznik_3_out_4[2]);
  Hex_Digit_Display hex_digit_display_3 (.value(licznik_4_out_4));  // open: dp
  and and_4 (and_4_out, and_2_out, and_5_out);
  and and_5 (and_5_out, licznik_3_out_4[0], not_6_out, not_7_out, licznik_3_out_4[3]);
  Hex_Digit_Display hex_digit_display_4 (.value(licznik_3_out_4));  // open: dp
  or or_2 (or_2_out, and_6_out, in_2);
  licznik licznik_4 (.EN(and_4_out), .clk(clock_1_out), .reset(or_2_out), .out_4(licznik_4_out_4));
  not not_8 (not_8_out, licznik_4_out_4[2]);
  not not_9 (not_9_out, licznik_4_out_4[3]);
  and and_6 (and_6_out, and_4_out, and_7_out);
  and and_7 (and_7_out, licznik_4_out_4[0], licznik_4_out_4[1], not_8_out, not_9_out);
  Hex_Digit_Display hex_digit_display_5 (.value(licznik_5_out_4));  // open: dp
  licznik licznik_5 (.EN(and_6_out), .clk(clock_1_out), .reset(in_2), .out_4(licznik_5_out_4));
endmodule

module licznik (
  input  EN,
  input  clk,
  input  reset,
  output [3:0] out_4
);

  wire and_1_out, and_2_out, and_3_out, and_4_out, and_5_out, not_1_out, not_2_out, or_1_out;

  or or_1 (or_1_out, reset, and_5_out);
  and and_1 (and_1_out, EN, or_1_out);
  sync_t sync_t_1 (.T(EN), .zero(and_1_out), .clk(clk), .Q(out_4[0]));
  and and_2 (and_2_out, EN, out_4[0]);
  sync_t sync_t_2 (.T(and_2_out), .zero(and_1_out), .clk(clk), .Q(out_4[1]));
  and and_3 (and_3_out, and_2_out, out_4[1]);
  sync_t sync_t_3 (.T(and_3_out), .zero(and_1_out), .clk(clk), .Q(out_4[2]));
  and and_4 (and_4_out, and_3_out, out_4[2]);
  sync_t sync_t_4 (.T(and_4_out), .zero(and_1_out), .clk(clk), .Q(out_4[3]));
  not not_1 (not_1_out, out_4[1]);
  and and_5 (and_5_out, out_4[0], not_1_out, not_2_out, out_4[3]);
  not not_2 (not_2_out, out_4[2]);
endmodule

module sync_t (
  input  T,
  input  zero,
  input  clk,
  output Q
);

  wire and_1_out, and_2_out, d_ff_1_qn, not_1_out, not_2_out, or_1_out;

  not not_1 (not_1_out, T);
  not not_2 (not_2_out, zero);
  and and_1 (and_1_out, T, d_ff_1_qn, not_2_out);
  and and_2 (and_2_out, not_2_out, Q, not_1_out);
  or or_1 (or_1_out, and_1_out, and_2_out);
  D_Flip_Flop d_ff_1 (.D(or_1_out), .clk(clk), .Q(Q), .Qn(d_ff_1_qn));  // open: preset, reset
endmodule

module licznik_D (
  input  D,
  input  R,
  input  clk,
  output Q
);

  wire and_1_out, not_1_out;

  and and_1 (and_1_out, D, not_1_out);
  not not_1 (not_1_out, R);
  D_Flip_Flop d_ff_1 (.D(and_1_out), .clk(clk), .Q(Q));  // open: Qn, preset, reset
endmodule

module sync_d (
  input  D,
  input  reset,
  input  clk,
  output Q
);

  wire and_1_out, not_1_out;

  D_Flip_Flop d_ff_1 (.D(and_1_out), .clk(clk), .Q(Q));  // open: Qn, preset, reset
  and and_1 (and_1_out, D, not_1_out);
  not not_1 (not_1_out, reset);
endmodule
