// Logisim project max_diff.circ as structural Verilog: 1 circuit, main circuit main
module main (
);

  wire clock_1_out, comparator_1_eq, comparator_1_lt, decoder_1_out0, decoder_1_out1, decoder_1_out2,
       decoder_1_out3;
  wire [1:0] dipswitch_3_sw2, dipswitch_4_sw2, undriven;
  wire [7:0] adder_1_out, multiplexer_1_out, multiplexer_2_out, not_1_out, register_1_q, register_2_q,
       register_3_q, register_4_q, register_5_q, undriven_2;

  // DipSwitch dipswitch_1: pin names not known
  // DipSwitch #(.number(2)) dipswitch_2: pin names not known
  Decoder #(.select(2)) decoder_1 (
    .out0(decoder_1_out0), .out1(decoder_1_out1), .out2(decoder_1_out2), .out3(decoder_1_out3), .sel(undriven));  // open: en
  Clock clock_1 (.out(clock_1_out));
  Register register_1 (.D(undriven_2), .en(decoder_1_out0), .clk(clock_1_out), .Q(register_1_q));  // open: clr
  Register register_2 (.D(undriven_2), .en(decoder_1_out1), .clk(clock_1_out), .Q(register_2_q));  // open: clr
  Register register_3 (.D(undriven_2), .en(decoder_1_out2), .clk(clock_1_out), .Q(register_3_q));  // open: clr
  Register register_4 (.D(undriven_2), .en(decoder_1_out3), .clk(clock_1_out), .Q(register_4_q));  // open: clr
  Multiplexer #(.select(2), .width(8)) multiplexer_1 (
    .in0(register_1_q), .in1(register_2_q), .in2(register_3_q), .in3(register_4_q), .out(multiplexer_1_out),
    .sel(dipswitch_3_sw2));
  DipSwitch #(.number(2)) dipswitch_3 (.sw1(dipswitch_3_sw2[1]), .sw2(dipswitch_3_sw2[0]));
  Multiplexer #(.select(2), .width(8)) multiplexer_2 (
    .in0(register_1_q), .in1(register_2_q), .in2(register_3_q), .in3(register_4_q), .out(multiplexer_2_out),
    .sel(dipswitch_4_sw2));
  DipSwitch #(.number(2)) dipswitch_4 (.sw1(dipswitch_4_sw2[1]), .sw2(dipswitch_4_sw2[0]));
  assign not_1_out = ~multiplexer_2_out;  // NOT_Gate not_1, 8 bits wide
  Register register_5 (.D(adder_1_out), .en(comparator_1_lt), .clk(clock_1_out), .Q(register_5_q));  // open: clr
  Adder adder_1 (.a(multiplexer_1_out), .b(not_1_out), .out(adder_1_out), .cin(1'b1));  // open: cout
  Comparator comparator_1 (.a(register_5_q), .b(adder_1_out), .eq(comparator_1_eq), .lt(comparator_1_lt));  // open: gt
  Hex_Digit_Display hex_digit_display_1 (.value(adder_1_out[7:4]));  // open: dp
  Hex_Digit_Display hex_digit_display_2 (.value(adder_1_out[3:0]));  // open: dp
endmodule
