// Logisim project mnozenie.circ as structural Verilog: 1 circuit, main circuit main
module main (
  input  write,
  input  in_2,
  input  add,
  output koniec
);

  wire clock_1_out, not_1_out, shift_register_1_p1, shift_register_1_p2, shift_register_1_p4;
  wire [3:0] A_q, counter_1_q, shift_register_1_p9, shift_register_1_p13, shift_register_2_p8,
       shift_register_2_p12, undriven;

  Clock clock_1 (.out(clock_1_out));
  Register #(.width(1)) register_1 ();  // open: D, en, clk, Q, clr
  Counter #(.max('hf), .width(4)) counter_1 (
    .load(write), .up(in_2), .count(not_1_out), .clk(clock_1_out), .D(4'b0100), .Q(counter_1_q));  // open: clr, carry
  nor nor_1 (koniec, counter_1_q[3], counter_1_q[2], counter_1_q[1], counter_1_q[0]);
  // DipSwitch #(.number(4)) dipswitch_1: pin names not known
  Register #(.width(4)) A (.D(undriven), .en(write), .clk(clock_1_out), .Q(A_q));  // open: clr
  Hex_Digit_Display hex_digit_display_1 (.value(undriven));  // open: dp
  // Shift_Register #(.length(4)) shift_register_1: pin names not known; wires that end beside it: shift_register_1_p1, shift_register_1_p2, write, shift_register_1_p4, shift_register_1_p1, shift_register_1_p9[3], shift_register_1_p9[2], shift_register_1_p9[1], shift_register_1_p9[0], shift_register_1_p13[3], shift_register_1_p13[2], shift_register_1_p13[1], shift_register_1_p13[0]
  Adder #(.width(4)) adder_1 (
    .a(shift_register_1_p13), .b(A_q), .out(shift_register_1_p9), .cout(shift_register_1_p2));  // open: cin
  // DipSwitch #(.number(4)) dipswitch_2: pin names not known
  and and_1 (shift_register_1_p4, shift_register_2_p12[0], add);
  not not_1 (not_1_out, add);
  Hex_Digit_Display hex_digit_display_2 (.value(shift_register_2_p8));  // open: dp
  // Shift_Register #(.length(4)) shift_register_2: pin names not known; wires that end beside it: write, not_1_out, clock_1_out, shift_register_1_p13[0], shift_register_2_p8[3], shift_register_2_p8[2], shift_register_2_p8[1], shift_register_2_p8[0], shift_register_2_p12[3], shift_register_2_p12[2], shift_register_2_p12[1], shift_register_2_p12[0]
  Hex_Digit_Display hex_digit_display_3 (.value(shift_register_1_p13));  // open: dp
  Hex_Digit_Display hex_digit_display_4 (.value(shift_register_2_p12));  // open: dp
endmodule
