// Logisim project pierwsza.circ as structural Verilog: 1 circuit, main circuit main
module main (
  input  in_1,
  output nast,
  output pierwsza,
  output koniec
);

  wire clock_1_out, nor_1_out, nor_2_out, s_r_ff_1_q, xor_1_out;
  wire [7:0] A_q, adder_1_out, counter_1_q, multiplexer_1_out, not_1_out, register_1_q, undriven;

  Clock clock_1 (.out(clock_1_out));
  // DipSwitch dipswitch_1: pin names not known
  Hex_Digit_Display hex_digit_display_1 (.value(undriven[7:4]));  // open: dp
  Register A (.D(undriven), .en(in_1), .clk(clock_1_out), .Q(A_q));  // open: clr
  Hex_Digit_Display hex_digit_display_2 (.value(undriven[3:0]));  // open: dp
  Counter counter_1 (
    .load(in_1), .D(undriven), .count(nast), .Q(counter_1_q), .up(1'b0), .clk(clock_1_out));  // open: carry, clr
  Register register_1 (.D(multiplexer_1_out), .clk(clock_1_out), .Q(register_1_q));  // open: en, clr
  Multiplexer #(.width(8)) multiplexer_1 (.in0(adder_1_out), .in1(A_q), .out(multiplexer_1_out), .sel(nast));
  assign not_1_out = ~counter_1_q;  // NOT_Gate not_1, 8 bits wide
  nor nor_1 (nor_1_out, counter_1_q[6], counter_1_q[5], counter_1_q[4], counter_1_q[3], counter_1_q[2], counter_1_q[1], ~counter_1_q[0]);  // NOR_Gate
  Adder adder_1 (.a(register_1_q), .b(not_1_out), .out(adder_1_out), .cin(1'b1));  // open: cout
  xor xor_1 (xor_1_out, register_1_q[7], adder_1_out[7]);
  nor nor_2 (nor_2_out, adder_1_out[7], adder_1_out[6], adder_1_out[5], adder_1_out[4], adder_1_out[3], adder_1_out[2], adder_1_out[1], adder_1_out[0]);
  or or_1 (nast, xor_1_out, nor_2_out);
  S_R_Flip_Flop s_r_ff_1 (
    .S(nor_2_out), .R(in_1), .clk(clock_1_out), .Q(s_r_ff_1_q), .Qn(pierwsza));  // open: reset, preset
  or or_2 (koniec, s_r_ff_1_q, nor_1_out);
endmodule
