// Logisim project srednia.circ as structural Verilog: 1 circuit, main circuit main
module main (
  input  load,
  output koniec,
  output dziel
);

  wire and_1_out, clock_1_out, not_1_out, not_2_out, not_3_out;
  wire [3:0] shift_register_1_p17, shift_register_1_p21;
  wire [7:0] A_q, adder_1_out, adder_2_out, multiplexer_1_out, R2_q, R_dzielenie_p12, R_dzielenie_p20,
       rom_1_data, undriven;

  // DipSwitch dipswitch_1: pin names not known
  // DipSwitch dipswitch_2: pin names not known
  Clock clock_1 (.out(clock_1_out));
  Multiplexer #(.width(8)) multiplexer_1 (.in0(undriven), .in1(adder_1_out), .out(multiplexer_1_out), .sel(not_1_out));
  not not_1 (not_1_out, load);
  Register A (.D(multiplexer_1_out), .en(not_2_out), .clk(clock_1_out), .Q(A_q));  // open: clr
  Counter R2 (
    .load(load), .up(1'b0), .count(not_2_out), .clk(clock_1_out), .D(R_dzielenie_p12), .Q(R2_q));  // open: clr, carry
  Adder adder_1 (.a(A_q), .b(8'h1), .out(adder_1_out));  // open: cin, cout
  // Shift_Register R_dzielenie: pin names not known; wires that end beside it: load, dziel, clock_1_out, 1'b0, R_dzielenie_p12[7], R_dzielenie_p12[6], R_dzielenie_p12[5], R_dzielenie_p12[4], R_dzielenie_p12[3], R_dzielenie_p12[2], R_dzielenie_p12[1], R_dzielenie_p12[0], R_dzielenie_p20[7], R_dzielenie_p20[6], R_dzielenie_p20[5], R_dzielenie_p20[4], R_dzielenie_p20[3], R_dzielenie_p20[2], R_dzielenie_p20[1], R_dzielenie_p20[0]
  ROM rom_1 (.addr(A_q), .data(rom_1_data));
  not not_2 (not_2_out, dziel);
  nor nor_1 (dziel, R2_q[0], R2_q[1], R2_q[2], R2_q[3], R2_q[4], R2_q[5], R2_q[6], R2_q[7]);
  nor nor_2 (koniec, ~R_dzielenie_p20[0], R_dzielenie_p20[1], R_dzielenie_p20[2], R_dzielenie_p20[3], R_dzielenie_p20[4], R_dzielenie_p20[5], R_dzielenie_p20[6], R_dzielenie_p20[7]);  // NOR_Gate
  not not_3 (not_3_out, rom_1_data[0]);
  Adder adder_2 (
    .a({shift_register_1_p17, shift_register_1_p21}), .b(rom_1_data), .out(adder_2_out));  // open: cin, cout
  and and_1 (and_1_out, not_3_out, ~dziel);  // AND_Gate
  // Shift_Register shift_register_1: pin names not known; wires that end beside it: load, and_1_out, dziel, clock_1_out, 1'b0, adder_2_out[7], adder_2_out[6], adder_2_out[5], adder_2_out[4], adder_2_out[3], adder_2_out[2], adder_2_out[1], adder_2_out[0], shift_register_1_p17[3], shift_register_1_p17[2], shift_register_1_p17[1], shift_register_1_p17[0], shift_register_1_p21[3], shift_register_1_p21[2], shift_register_1_p21[1], shift_register_1_p21[0]
  Hex_Digit_Display hex_digit_display_1 (.value(shift_register_1_p17));  // open: dp
  Hex_Digit_Display hex_digit_display_2 (.value(shift_register_1_p21));  // open: dp

  // Notes on the sheet:
  //   contents of rom_1 (hex, n*v repeats v):
  //   1 2 3 a fc
endmodule
